// Logisim project cpu1.circ as structural Verilog
module main (
  input  in_1,
  input  in_2,
  input  in_3,
  input  in_4
);

  wire and_1_out, and_2_out, button_1_out, button_2_out, controlled_buffer_1_out;

  and and_1 (and_1_out, in_1, in_2);
  and and_2 (and_2_out, in_3, in_4);
  assign controlled_buffer_1_out = button_1_out ? and_1_out : 1'bz;  // Controlled_Buffer controlled_buffer_1
  assign controlled_buffer_1_out = button_2_out ? and_2_out : 1'bz;  // Controlled_Buffer controlled_buffer_2
  Button button_1 (.out(button_1_out));
  Button button_2 (.out(button_2_out));
endmodule

module memory_1 (
  input  s,
  input  e,
  output q
);

  wire nand_1_out, nand_2_out, nand_4_out;

  nand nand_1 (nand_1_out, s, e);
  nand nand_2 (nand_2_out, nand_1_out, e);
  nand nand_3 (q, nand_1_out, nand_4_out);
  nand nand_4 (nand_4_out, q, nand_2_out);

  // Notes on the sheet:
  //   1 bit memory cell
endmodule

module memory_8 (
  input  [7:0] in_1,
  input  in_2,
  output [7:0] out_3
);

  memory_1 memory_1_1 (.s(in_1[0]), .e(in_2), .q(out_3[0]));
  memory_1 memory_1_2 (.s(in_1[1]), .e(in_2), .q(out_3[1]));
  memory_1 memory_1_3 (.s(in_1[2]), .e(in_2), .q(out_3[2]));
  memory_1 memory_1_4 (.s(in_1[3]), .e(in_2), .q(out_3[3]));
  memory_1 memory_1_5 (.s(in_1[4]), .e(in_2), .q(out_3[4]));
  memory_1 memory_1_6 (.s(in_1[5]), .e(in_2), .q(out_3[5]));
  memory_1 memory_1_7 (.s(in_1[6]), .e(in_2), .q(out_3[6]));
  memory_1 memory_1_8 (.s(in_1[7]), .e(in_2), .q(out_3[7]));
endmodule

module cpu_enable (
  input  [7:0] I,
  input  E,
  output [7:0] O
);

  wire and_8_out;

  and and_1 (O[0], I[0], E);
  and and_2 (O[1], I[1], E);
  and and_3 (O[2], I[2], E);
  and and_4 (O[3], I[3], E);
  and and_5 (O[4], I[4], E);
  and and_6 (O[5], I[5], E);
  and and_7 (O[6], I[6], E);
  and and_8 (and_8_out, I[7], E);
  assign O[0] = E ? O[0] : 1'bz;  // Controlled_Buffer controlled_buffer_1
  assign O[1] = E ? O[1] : 1'bz;  // Controlled_Buffer controlled_buffer_2
  assign O[2] = E ? O[2] : 1'bz;  // Controlled_Buffer controlled_buffer_3
  assign O[3] = E ? O[3] : 1'bz;  // Controlled_Buffer controlled_buffer_4
  assign O[4] = E ? O[4] : 1'bz;  // Controlled_Buffer controlled_buffer_5
  assign O[5] = E ? O[5] : 1'bz;  // Controlled_Buffer controlled_buffer_6
  assign O[6] = E ? O[6] : 1'bz;  // Controlled_Buffer controlled_buffer_7
  assign O[7] = E ? and_8_out : 1'bz;  // Controlled_Buffer controlled_buffer_8
endmodule

module cpu_reg_8 (
  input  [7:0] in_1,
  input  s,
  input  e,
  output [7:0] out_4,
  output [7:0] out_5
);

  wire [7:0] cpu_enable_1_o;

  memory_8 memory_8_1 (.in_1(in_1), .out_3(out_4), .in_2(s));
  cpu_enable cpu_enable_1 (.I(out_4), .E(e), .O(cpu_enable_1_o));
  assign out_5 = e ? cpu_enable_1_o : 8'bz;  // Controlled_Buffer controlled_buffer_1

  // Notes on the sheet:
  //   i
  //   reg
endmodule

module cpu_reg_byte (
  input  [7:0] in_1,
  input  reset,
  input  [7:0] \İ ,
  input  h,
  input  v,
  input  s,
  input  e,
  output [7:0] out_8
);

  wire and_1_out, and_2_out, and_3_out, or_1_out;
  wire [7:0] cpu_reg_8_1_out_5;

  and and_1 (and_1_out, h, v);
  and and_2 (and_2_out, and_1_out, s);
  and and_3 (and_3_out, and_1_out, e);
  or or_1 (or_1_out, reset, and_2_out);
  cpu_reg_8 cpu_reg_8_1 (.in_1(\İ ), .s(or_1_out), .e(and_3_out), .out_5(cpu_reg_8_1_out_5), .out_4(in_1));
  assign out_8 = and_3_out ? cpu_reg_8_1_out_5 : 8'bz;  // Controlled_Buffer controlled_buffer_1
endmodule

module cpu_decoder_4x16 (
  input  [3:0] in_1,
  output _0,
  output _1,
  output _2,
  output _3,
  output _4,
  output _5,
  output _6,
  output _7,
  output _8,
  output _9,
  output _10,
  output _11,
  output _12,
  output _13,
  output _14,
  output _15
);

  wire not_1_out, not_2_out, not_3_out, not_4_out;

  not not_1 (not_1_out, in_1[3]);
  not not_2 (not_2_out, in_1[2]);
  not not_3 (not_3_out, in_1[1]);
  not not_4 (not_4_out, in_1[0]);
  and and_1 (_0, not_4_out, not_3_out, not_2_out, not_1_out);
  and and_2 (_1, not_4_out, not_3_out, not_2_out, in_1[3]);
  and and_3 (_2, not_4_out, not_3_out, in_1[2], not_1_out);
  and and_4 (_3, not_4_out, not_2_out, in_1[2], in_1[3]);
  and and_5 (_4, not_4_out, in_1[1], not_2_out, not_1_out);
  and and_6 (_5, not_4_out, in_1[1], not_2_out, in_1[3]);
  and and_7 (_6, not_4_out, in_1[1], in_1[2], not_1_out);
  and and_8 (_7, not_4_out, in_1[1], in_1[2], in_1[3]);
  and and_9 (_8, in_1[0], not_3_out, not_2_out, not_1_out);
  and and_10 (_9, in_1[0], not_3_out, not_2_out, in_1[3]);
  and and_11 (_10, in_1[0], not_3_out, in_1[2], not_1_out);
  and and_12 (_11, in_1[0], not_3_out, in_1[2], in_1[3]);
  and and_13 (_12, in_1[0], in_1[1], not_2_out, not_1_out);
  and and_14 (_13, in_1[0], in_1[1], not_2_out, in_1[3]);
  and and_15 (_14, in_1[0], in_1[1], in_1[2], not_1_out);
  and and_16 (_15, in_1[0], in_1[1], in_1[2], in_1[3]);

  // Notes on the sheet:
  //   0
  //   1
  //   2
  //   3
endmodule
